# Fritzing sketch TCapChamp (saved by Fritzing 1.0.2b)
breadboards: 1

parts:
  Output_Temperature = MCP4151-503E/P [part_number=MCP4151-503E/P package=MCP4151]
  ESP32_NodeMCU-32S = ESP32S-HiLetgo [part_number=ESP32S-HiLetgo]
  Temperature_Out = Camdenboss CTB0158-2 [part_number=CTB0158-2 package=THT]
  Temperature_In = Camdenboss CTB0158-2 [part_number=CTB0158-2 package=THT]
  Voltage_devider_ref = Resistor [tolerance=±5% resistance=10k package="0402 [SMD]"]
  Ext_Temp_Sensor = Temperature Sensor (Thermistor) [thermistor_type=NTC package=THT]
  Heat_pump_(Temperature) = Multimeter (Ohmmeter)
  Preresistor = Resistor [tolerance=±5% power=0.25W resistance=4.7k package=THT]
  DAC_0-10V = MCP4725 [package=SOT23-6]
  Heat_pump_(power_Limit_0-10V) = Multimeter (DC Voltage)
  GND_Pulldown = Resistor [tolerance=±5% resistance=2.2k package="0402 [SMD]"]

nets:
  N1: Output_Temperature.CS, ESP32_NodeMCU-32S.GPIO5
  N2: Output_Temperature.SCK, ESP32_NodeMCU-32S.GPIO18
  N3: Output_Temperature.SDI/SDO, ESP32_NodeMCU-32S.GPIO23
  VSS: Output_Temperature.Vss, ESP32_NodeMCU-32S.GND, Temperature_In.pin1, DAC_0-10V.VSS, GND_Pulldown.Pin_0
  N4: Output_Temperature.P0A, GND_Pulldown.Pin_1
  N5: Output_Temperature.P0W, Temperature_Out.pin2
  N6: Output_Temperature.P0B, Preresistor.Pin_1
  N7: Output_Temperature.Vdd, ESP32_NodeMCU-32S.3.3, Voltage_devider_ref.Pin_0
  N8: ESP32_NodeMCU-32S.GPIO36, Temperature_In.pin2, Voltage_devider_ref.Pin_1
  VIN: ESP32_NodeMCU-32S.VIN, DAC_0-10V.VDD
  N9: ESP32_NodeMCU-32S.GPIO21, DAC_0-10V.SDA
  N10: ESP32_NodeMCU-32S.GPIO22, DAC_0-10V.SCL
  N11: Temperature_Out.pin1, Preresistor.Pin_0
  N12: Temperature_Out.terminal_1, Heat_pump_(Temperature).COM_Probe
  N13: Temperature_Out.terminal_2, Heat_pump_(Temperature).V_Probe
  N14: Temperature_In.terminal_1, Ext_Temp_Sensor.pin_0
  N15: Temperature_In.terminal_2, Ext_Temp_Sensor.pin_1
  N16: DAC_0-10V.VOUT, Heat_pump_(power_Limit_0-10V).COM_Probe
  N17: DAC_0-10V.AO, Heat_pump_(power_Limit_0-10V).V_Probe

custom parts:
  MCP4151-503E/P: The MCP4151 Dallastat is a nonvolatile digitally controlled potentiometer that provides 257 uniform wiper positions over the entire resistor range; including the high-end and low-end terminals of the device. The MCP4151 is a low-power device capable of operating from power supplies of +1.8V to +5.5V. The device is ideal for low-power, portable, or battery powered applications.
  ESP32S-HiLetgo: HiLetgo ESP-WROOM-32 ESP32 ESP-32S Development Board 2.4GHz Dual-Mode WiFi + Bluetooth Dual Cores Microcontroller The ESP32 integrated with Antenna switches, RF Balun, power amplifiers, low-noise amplifiers, filters, and management modules, and the entire solution occupies the least area of PCB. 2.4 GHz Wi-Fi plus Bluetooth dual-mode chip, with TSMC Ultra-low power consumption 40nm technology,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
